// Logisim project cpu.circ as structural Verilog: 13 circuits, main circuit main
// 2
module main (
  input  [31:0] RS_READ_VALUE,
  input  [31:0] RI_READ_VALUE,
  input  [31:0] RD_READ_VALUE,
  input  [31:0] JC_READ_VALUE,
  input  [31:0] INSTRUCTION,
  input  CLOCK,
  output [4:0] RS,
  output [4:0] RI,
  output [4:0] RD,
  output [31:0] RD_WRITE_VALUE,
  output RD_WRITE_ENABLE,
  output [23:0] FETCH_ADDRESS
);

  wire and_1_out, comparator_2_eq, comparator_3_eq, comparator_4_eq, comparator_5_eq, comparator_6_eq,
       comparator_7_eq, comparator_8_eq, FIRST_BIT, J_INSTR, JAL, MEM_TO_REG, MEM_W, N_J, N_M_N_J, N_MEM_W,
       WORD;
  wire [23:0] adder_1_out, bit_extender_2_out, J_PC, multiplexer_3_out;
  wire [24:0] bit_extender_4_out;
  wire [31:0] ALU_OUTPUT, bit_extender_3_out, MEM_OUTPUT, multiplexer_5_out, multiplexer_6_out, OUTPUT, PC_1;

  Multiplexer #(.width(5)) multiplexer_1 (.in0(INSTRUCTION[26:22]), .in1(5'b00110), .out(RD), .sel(JAL));  // open: en
  Multiplexer #(.width(32)) multiplexer_2 (.in0(OUTPUT), .in1(PC_1), .out(RD_WRITE_VALUE), .sel(JAL));  // open: en
  or or_1 (RD_WRITE_ENABLE, N_M_N_J, JAL);
  // Probe on J_INSTR
  Adder #(.width(24)) adder_1 (.a(FETCH_ADDRESS), .b(24'h1), .out(adder_1_out));  // open: cin, cout
  and and_1 (and_1_out, J_INSTR, FIRST_BIT);
  and and_2 (N_M_N_J, N_MEM_W, N_J);
  assign PC_1 = {{8{1'b0}}, adder_1_out};  // Bit_Extender bit_extender_1
  Multiplexer #(.width(24)) multiplexer_3 (
    .in0(adder_1_out), .in1(J_PC), .out(multiplexer_3_out), .sel(and_1_out));  // open: en
  Register #(.width(24)) PC (.D(multiplexer_3_out), .Q(FETCH_ADDRESS), .clk(CLOCK));  // open: en, clr
  // Probe on INSTRUCTION[26:24]
  Bit_Extender #(.in_width(32), .out_width(24)) bit_extender_2 (.in(RI_READ_VALUE), .out(bit_extender_2_out));
  Comparator #(.width(4)) comparator_1 (.a(INSTRUCTION[31:28]), .b(4'b1111), .eq(J_INSTR));  // open: gt, lt
  Comparator #(.width(3)) comparator_2 (.a(INSTRUCTION[26:24]), .b(3'b111), .eq(comparator_2_eq));  // open: gt, lt
  assign bit_extender_3_out = {{15{INSTRUCTION[16]}}, INSTRUCTION[16:0]};  // Bit_Extender bit_extender_3
  Bit_Extender #(.in_width(32), .out_width(25)) bit_extender_4 (.in(ALU_OUTPUT), .out(bit_extender_4_out));
  Multiplexer #(.width(24)) multiplexer_4 (
    .in0(bit_extender_2_out), .in1(INSTRUCTION[23:0]), .out(J_PC), .sel(INSTRUCTION[27]));  // open: en
  Bit_Extender #(.in_width(32), .out_width(1)) bit_extender_5 (.in(ALU_OUTPUT), .out(FIRST_BIT));
  and and_3 (JAL, J_INSTR, comparator_2_eq);
  Multiplexer #(.width(32)) multiplexer_5 (
    .in0(RS_READ_VALUE), .in1(JC_READ_VALUE), .out(multiplexer_5_out), .sel(J_INSTR));  // open: en
  Multiplexer #(.width(32)) multiplexer_6 (
    .in0(RI_READ_VALUE), .in1(bit_extender_3_out), .out(multiplexer_6_out), .sel(INSTRUCTION[27]));  // open: en
  u_ALU u_alu_1 (
    .ALU_X(multiplexer_5_out), .ALU_Y(multiplexer_6_out), .ALU_RESULT(ALU_OUTPUT),
    .ALU_CONTROL(INSTRUCTION[31:28]), .JOP(INSTRUCTION[26:24]));
  u_MEM u_mem_1 (
    .ADDRESS(bit_extender_4_out), .WORD_MODE(WORD), .MEM_WRITE(MEM_W), .DATA_IN(RD_READ_VALUE),
    .CLOCK(CLOCK), .DATA_OUT(MEM_OUTPUT));
  Multiplexer #(.width(32)) multiplexer_7 (
    .in0(ALU_OUTPUT), .in1(MEM_OUTPUT), .out(OUTPUT), .sel(MEM_TO_REG));  // open: en
  Comparator #(.width(4)) comparator_3 (.a(INSTRUCTION[31:28]), .b(4'b1010), .eq(comparator_3_eq));  // open: gt, lt
  Comparator #(.width(4)) comparator_4 (.a(INSTRUCTION[31:28]), .b(4'b1100), .eq(comparator_4_eq));  // open: gt, lt
  Comparator #(.width(4)) comparator_5 (.a(INSTRUCTION[31:28]), .b(4'b1011), .eq(comparator_5_eq));  // open: gt, lt
  Comparator #(.width(4)) comparator_6 (.a(INSTRUCTION[31:28]), .b(4'b1101), .eq(comparator_6_eq));  // open: gt, lt
  not not_1 (N_J, J_INSTR);
  // Probe on ALU_OUTPUT
  Comparator #(.width(4)) comparator_7 (.a(INSTRUCTION[31:28]), .b(4'b1100), .eq(comparator_7_eq));  // open: gt, lt
  Comparator #(.width(4)) comparator_8 (.a(INSTRUCTION[31:28]), .b(4'b1101), .eq(comparator_8_eq));  // open: gt, lt
  or or_2 (MEM_TO_REG, comparator_3_eq, comparator_4_eq);
  not not_2 (N_MEM_W, MEM_W);
  or or_3 (WORD, comparator_7_eq, comparator_8_eq);
  or or_4 (MEM_W, comparator_5_eq, comparator_6_eq);

  assign RI = INSTRUCTION[4:0];
  assign RS = INSTRUCTION[21:17];

  // Other names for the same wires on the sheet: ADDR[23:0] = FETCH_ADDRESS; CLK = CLOCK; _27 = INSTRUCTION[27];
  //   OP[3:0] = INSTRUCTION[31:28]; _0_4[4:0] = INSTRUCTION[4:0]; IMM[16:0] = INSTRUCTION[16:0];
  //   J_IMM[23:0] = INSTRUCTION[23:0]; _5_16[11:0] = INSTRUCTION[16:5]; RD_t[4:0] = INSTRUCTION[26:22];
  //   JC_READ[31:0] = JC_READ_VALUE; RD_READ[31:0] = RD_READ_VALUE; J_OP[2:0] = INSTRUCTION[26:24];
  //   RI_READ[31:0] = RI_READ_VALUE; RS_READ[31:0] = RS_READ_VALUE
endmodule

module u_ALU (
  input  [31:0] ALU_X,
  input  [31:0] ALU_Y,
  input  [2:0] JOP,
  input  [3:0] ALU_CONTROL,
  output [31:0] ALU_RESULT
);

  wire comparator_1_eq, comparator_1_gt, comparator_1_lt, multiplexer_2_out, not_1_out, not_2_out, not_3_out;
  wire [4:0] bit_extender_1_out;
  wire [14:0] bit_extender_2_out;
  wire [16:0] bit_extender_3_out;
  wire [31:0] ADD, AND, DIV, J_OUTPUT, LHW, MUL, OR, REV, SL, SR, STU, SUB, X_0_14, XOR, Y_0_16, Y_17_31;

  Bit_Extender #(.in_width(32), .out_width(5)) bit_extender_1 (.in(ALU_Y), .out(bit_extender_1_out));
  Adder #(.width(32)) adder_1 (.a(ALU_X), .b(ALU_Y), .out(LHW));  // open: cin, cout
  Bit_Extender #(.in_width(32), .out_width(15)) bit_extender_2 (.in(ALU_X), .out(bit_extender_2_out));
  Bit_Extender #(.in_width(32), .out_width(17)) bit_extender_3 (.in(ALU_Y), .out(bit_extender_3_out));
  u_SL u_sl_1 (.INPUT1(ALU_X), .INPUT2(bit_extender_1_out), .OUT(SL));
  Shifter #(.width(32), .shift("ar")) shifter_1 (.in(ALU_X), .\dist (bit_extender_1_out), .out(SR));
  assign AND = ALU_X & ALU_Y;  // AND_Gate and_1, 32 bits wide
  assign OR = ALU_X | ALU_Y;  // OR_Gate or_1, 32 bits wide
  u_REV u_rev_1 (.INPUT(ALU_X), .OUTPUT(REV), .REVERSE_AMOUNT(bit_extender_1_out));
  assign XOR = ALU_X ^ ALU_Y;  // XOR_Gate xor_1, 32 bits wide
  Adder #(.width(32)) adder_2 (.a(ALU_X), .b(ALU_Y), .out(ADD));  // open: cin, cout
  Subtractor #(.width(32)) subtractor_1 (.a(ALU_X), .b(ALU_Y), .out(SUB));  // open: bin, bout
  Multiplier #(.width(32)) multiplier_1 (.a(ALU_X), .b(ALU_Y), .out(MUL));  // open: cin, cout
  u_DIV u_div_1 (.X(ALU_X), .Y(ALU_Y), .out_3(DIV));
  assign X_0_14 = {{17{1'b0}}, bit_extender_2_out};  // Bit_Extender bit_extender_4
  assign Y_0_16 = {{15{1'b0}}, bit_extender_3_out};  // Bit_Extender bit_extender_5
  Shifter #(.width(32)) shifter_2 (.in(Y_0_16), .\dist (5'b01111), .out(Y_17_31));
  assign STU = X_0_14 | Y_17_31;  // OR_Gate or_2, 32 bits wide
  Comparator #(.width(32)) comparator_1 (
    .a(ALU_X), .b({32{1'b0}}), .gt(comparator_1_gt), .eq(comparator_1_eq), .lt(comparator_1_lt));
  not not_1 (not_1_out, comparator_1_eq);
  not not_2 (not_2_out, comparator_1_lt);
  // Probe on ALU_RESULT
  Multiplexer #(.select(4), .width(32)) multiplexer_1 (
    .in0(SL), .in1(SR), .in2(AND), .in3(OR), .in4(REV), .in5(XOR), .in6(ADD), .in7(SUB), .in8(MUL),
    .in9(DIV), .in10(LHW), .in11(LHW), .in12(LHW), .in13(LHW), .in14(STU), .in15(J_OUTPUT), .out(ALU_RESULT),
    .sel(ALU_CONTROL));  // open: en
  not not_3 (not_3_out, comparator_1_gt);
  Multiplexer #(.select(3)) multiplexer_2 (
    .in0(1'b1), .in1(comparator_1_gt), .in2(comparator_1_eq), .in3(comparator_1_lt), .in4(not_3_out),
    .in5(not_1_out), .in6(not_2_out), .in7(1'b1), .out(multiplexer_2_out), .sel(JOP));  // open: en
  // Probe on JOP
  assign J_OUTPUT = {{31{1'b0}}, multiplexer_2_out};  // Bit_Extender bit_extender_6

  // Other names for the same wires on the sheet: J[2:0] = JOP; LW[31:0] = LHW; SHW[31:0] = LHW; SW[31:0] = LHW;
  //   X[31:0] = ALU_X; Y[31:0] = ALU_Y
endmodule

// Data Memory
module u_MEM (
  input  [24:0] ADDRESS,
  input  WORD_MODE,
  input  MEM_WRITE,
  input  [31:0] DATA_IN,
  input  CLOCK,
  output [31:0] DATA_OUT
);

  wire not_1_out, not_2_out, not_3_out, or_1_out, or_2_out;
  wire [0:0] adder_1_out;
  wire [15:0] EVEN_OUT, multiplexer_5_out, multiplexer_6_out, multiplexer_9_out, multiplexer_11_out, ODD_OUT;
  wire [23:0] multiplexer_1_out, multiplexer_2_out, multiplexer_8_out, multiplexer_10_out, NEXT_ADDR;
  wire [31:0] bit_extender_1_out, bit_extender_2_out, multiplexer_3_out, multiplexer_4_out;

  Adder #(.width(25)) adder_1 (.a(ADDRESS), .b(25'h1), .out({NEXT_ADDR, adder_1_out[0]}));  // open: cin, cout
  assign bit_extender_1_out = {{16{EVEN_OUT[15]}}, EVEN_OUT};  // Bit_Extender bit_extender_1
  assign bit_extender_2_out = {{16{ODD_OUT[15]}}, ODD_OUT};  // Bit_Extender bit_extender_2
  Multiplexer #(.width(24)) multiplexer_1 (
    .in0(ADDRESS[24:1]), .in1(NEXT_ADDR), .out(multiplexer_1_out), .sel(ADDRESS[0]));  // open: en
  Multiplexer #(.width(24)) multiplexer_2 (
    .in0(NEXT_ADDR), .in1(ADDRESS[24:1]), .out(multiplexer_2_out), .sel(ADDRESS[0]));  // open: en
  Multiplexer #(.width(32)) multiplexer_3 (
    .in0(bit_extender_1_out), .in1({ODD_OUT, EVEN_OUT}), .out(multiplexer_3_out), .sel(WORD_MODE));  // open: en
  Multiplexer #(.width(32)) multiplexer_4 (
    .in0(bit_extender_2_out), .in1({EVEN_OUT, ODD_OUT}), .out(multiplexer_4_out), .sel(WORD_MODE));  // open: en
  Multiplexer #(.width(16)) multiplexer_5 (
    .in0(DATA_IN[15:0]), .in1(DATA_IN[31:16]), .out(multiplexer_5_out), .sel(ADDRESS[0]));  // open: en
  Multiplexer #(.width(16)) multiplexer_6 (
    .in0(DATA_IN[31:16]), .in1(DATA_IN[15:0]), .out(multiplexer_6_out), .sel(ADDRESS[0]));  // open: en
  Multiplexer #(.width(32)) multiplexer_7 (
    .in0(multiplexer_3_out), .in1(multiplexer_4_out), .out(DATA_OUT), .sel(ADDRESS[0]));  // open: en
  Multiplexer #(.width(24)) multiplexer_8 (
    .in0(ADDRESS[24:1]), .in1(multiplexer_1_out), .out(multiplexer_8_out), .sel(WORD_MODE));  // open: en
  Multiplexer #(.width(16)) multiplexer_9 (
    .in0(DATA_IN[15:0]), .in1(multiplexer_5_out), .out(multiplexer_9_out), .sel(WORD_MODE));  // open: en
  Multiplexer #(.width(24)) multiplexer_10 (
    .in0(ADDRESS[24:1]), .in1(multiplexer_2_out), .out(multiplexer_10_out), .sel(WORD_MODE));  // open: en
  Multiplexer #(.width(16)) multiplexer_11 (
    .in0(DATA_IN[15:0]), .in1(multiplexer_6_out), .out(multiplexer_11_out), .sel(WORD_MODE));  // open: en
  or or_1 (or_1_out, not_2_out, WORD_MODE);
  or or_2 (or_2_out, ADDRESS[0], WORD_MODE);
  RAM #(.addrWidth(24), .dataWidth(16), .bus("separate")) ram_1 (
    .addr(multiplexer_8_out), .din(multiplexer_9_out), .data(EVEN_OUT), .str(MEM_WRITE), .sel(or_1_out),
    .clk(CLOCK), .ld(not_1_out));  // open: clr
  not not_1 (not_1_out, MEM_WRITE);
  not not_2 (not_2_out, ADDRESS[0]);
  RAM #(.addrWidth(24), .dataWidth(16), .bus("separate")) ram_2 (
    .addr(multiplexer_10_out), .din(multiplexer_11_out), .data(ODD_OUT), .str(MEM_WRITE), .sel(or_2_out),
    .clk(CLOCK), .ld(not_3_out));  // open: clr
  not not_3 (not_3_out, MEM_WRITE);

  // Other names for the same wires on the sheet: CLK = CLOCK; LOWER[15:0] = DATA_IN[15:0];
  //   UPPER[15:0] = DATA_IN[31:16]; N_ADDR[24:0] = ADDRESS; ODD = ADDRESS[0]; ADDR[23:0] = ADDRESS[24:1];
  //   OUT[31:0] = DATA_OUT; W = MEM_WRITE; WORD = WORD_MODE
endmodule

module u_REV (
  input  [31:0] INPUT,
  input  [4:0] REVERSE_AMOUNT,
  output [31:0] OUTPUT
);

  wire [31:0] multiplexer_1_out, multiplexer_2_out, multiplexer_3_out, multiplexer_4_out, u_rev1_1_out_2,
       u_rev2_1_out_2, u_rev4_1_out_2, u_rev8_1_out_2, u_rev16_1_out_2;

  // Probe on INPUT
  Multiplexer #(.width(32)) multiplexer_1 (
    .in0(INPUT), .in1(u_rev1_1_out_2), .out(multiplexer_1_out), .sel(REVERSE_AMOUNT[0]));  // open: en
  u_REV1 u_rev1_1 (.A(INPUT), .out_2(u_rev1_1_out_2));
  u_REV2 u_rev2_1 (.A(multiplexer_1_out), .out_2(u_rev2_1_out_2));
  Multiplexer #(.width(32)) multiplexer_2 (
    .in0(multiplexer_1_out), .in1(u_rev2_1_out_2), .out(multiplexer_2_out), .sel(REVERSE_AMOUNT[1]));  // open: en
  u_REV4 u_rev4_1 (.A(multiplexer_2_out), .out_2(u_rev4_1_out_2));
  Multiplexer #(.width(32)) multiplexer_3 (
    .in0(multiplexer_2_out), .in1(u_rev4_1_out_2), .out(multiplexer_3_out), .sel(REVERSE_AMOUNT[2]));  // open: en
  u_REV8 u_rev8_1 (.A(multiplexer_3_out), .out_2(u_rev8_1_out_2));
  Multiplexer #(.width(32)) multiplexer_4 (
    .in0(multiplexer_3_out), .in1(u_rev8_1_out_2), .out(multiplexer_4_out), .sel(REVERSE_AMOUNT[3]));  // open: en
  Multiplexer #(.width(32)) multiplexer_5 (
    .in0(multiplexer_4_out), .in1(u_rev16_1_out_2), .out(OUTPUT), .sel(REVERSE_AMOUNT[4]));  // open: en
  u_REV16 u_rev16_1 (.A(multiplexer_4_out), .out_2(u_rev16_1_out_2));
  // Probe on OUTPUT
endmodule

module u_SL1 (
  input  [31:0] In,
  output [31:0] out_2
);

  wire [31:0] bit_extender_1_out, shifter_1_out;

  assign bit_extender_1_out = {{31{1'b0}}, In[0]};  // Bit_Extender bit_extender_1
  Shifter #(.width(32)) shifter_1 (.in(In), .\dist (5'b00001), .out(shifter_1_out));
  Adder #(.width(32)) adder_1 (.a(bit_extender_1_out), .b(shifter_1_out), .out(out_2));  // open: cin, cout
endmodule

module u_SL (
  input  [31:0] INPUT1,
  input  [4:0] INPUT2,
  output [31:0] OUT
);

  wire [4:0] subtractor_1_out;
  wire [31:0] multiplexer_1_out, not_1_out, shifter_1_out, shifter_2_out;

  Shifter #(.width(32)) shifter_1 (.in(INPUT1), .\dist (INPUT2), .out(shifter_1_out));
  Multiplexer #(.width(32)) multiplexer_1 (
    .in0({32{1'b0}}), .in1(not_1_out), .out(multiplexer_1_out), .sel(INPUT1[0]));  // open: en
  assign not_1_out = ~{32{1'b0}};  // NOT_Gate not_1, 32 bits wide
  Subtractor #(.width(5)) subtractor_1 (.a({5{1'b1}}), .b(INPUT2), .out(subtractor_1_out));  // open: bin, bout
  Shifter #(.width(32), .shift("lr")) shifter_2 (
    .in(multiplexer_1_out), .\dist (subtractor_1_out), .out(shifter_2_out));
  assign OUT = shifter_1_out | shifter_2_out;  // OR_Gate or_1, 32 bits wide
endmodule

module u_DIV (
  input  [31:0] X,
  input  [31:0] Y,
  output [31:0] out_3
);

  wire comparator_1_eq, comparator_2_eq, NEG;
  wire [31:0] adder_2_out, adder_3_out, div, dividend, divisor, INF, multiplexer_5_out, n_div, p_div,
       u_flipbits_1_out_2, u_flipbits_2_out_2, u_flipbits_3_out_2;

  // Probe on X
  // Probe on p_div
  Divider #(.width(32)) divider_1 (.a(dividend), .b(divisor), .out(p_div));  // open: upper, rem
  // Probe on u_flipbits_1_out_2
  u_FLIPBITS u_flipbits_1 (.in_1(p_div), .out_2(u_flipbits_1_out_2));
  Multiplexer #(.width(32)) multiplexer_1 (.in0(p_div), .in1(n_div), .out(div), .sel(NEG));  // open: en
  // Probe on Y
  // Probe on n_div
  Adder #(.width(32)) adder_1 (.a(u_flipbits_1_out_2), .b(32'h1), .out(n_div));  // open: cin, cout
  xor xor_1 (NEG, X[31], Y[31]);
  // Probe on NEG
  Multiplexer #(.width(32)) multiplexer_2 (.in0(32'h7fffffff), .in1(32'h80000000), .out(INF), .sel(X[31]));  // open: en
  // Probe on INF
  u_FLIPBITS u_flipbits_2 (.in_1(X), .out_2(u_flipbits_2_out_2));
  u_FLIPBITS u_flipbits_3 (.in_1(Y), .out_2(u_flipbits_3_out_2));
  Multiplexer #(.width(32)) multiplexer_3 (.in0(X), .in1(adder_2_out), .out(dividend), .sel(X[31]));  // open: en
  Adder #(.width(32)) adder_2 (.a(u_flipbits_2_out_2), .b(32'h1), .out(adder_2_out));  // open: cin, cout
  Multiplexer #(.width(32)) multiplexer_4 (.in0(Y), .in1(adder_3_out), .out(divisor), .sel(Y[31]));  // open: en
  Adder #(.width(32)) adder_3 (.a(u_flipbits_3_out_2), .b(32'h1), .out(adder_3_out));  // open: cin, cout
  Multiplexer #(.width(32)) multiplexer_5 (
    .in0(div), .in1(INF), .out(multiplexer_5_out), .sel(comparator_1_eq));  // open: en
  Comparator #(.width(32)) comparator_1 (.a(divisor), .b({32{1'b0}}), .eq(comparator_1_eq));  // open: gt, lt
  // Probe on dividend
  // Probe on divisor
  // Probe on multiplexer_5_out
  Comparator #(.width(32)) comparator_2 (.a(dividend), .b({32{1'b0}}), .eq(comparator_2_eq));  // open: gt, lt
  // Probe on out_3
  Multiplexer #(.width(32)) multiplexer_6 (
    .in0(multiplexer_5_out), .in1({32{1'b0}}), .out(out_3), .sel(comparator_2_eq));  // open: en

  // Other names for the same wires on the sheet: X_NEG = X[31]; Y_NEG = Y[31]
endmodule

module u_REV1 (
  input  [31:0] A,
  output [31:0] out_2
);


  assign out_2 = {A[30], A[31], A[28], A[29], A[26], A[27], A[24], A[25], A[22], A[23], A[20], A[21], A[18], A[19], A[16], A[17], A[14], A[15], A[12], A[13], A[10], A[11], A[8], A[9], A[6], A[7], A[4], A[5], A[2], A[3], A[0], A[1]};
endmodule

module u_REV2 (
  input  [31:0] A,
  output [31:0] out_2
);


  assign out_2 = {A[29:28], A[31:30], A[25:24], A[27:26], A[21:20], A[23:22], A[17:16], A[19:18], A[13:12], A[15:14], A[9:8], A[11:10], A[5:4], A[7:6], A[1:0], A[3:2]};
endmodule

module u_REV4 (
  input  [31:0] A,
  output [31:0] out_2
);


  assign out_2 = {A[27:24], A[31:28], A[19:16], A[23:20], A[11:8], A[15:12], A[3:0], A[7:4]};
endmodule

module u_REV8 (
  input  [31:0] A,
  output [31:0] out_2
);


  assign out_2 = {A[23:16], A[31:24], A[7:0], A[15:8]};
endmodule

module u_REV16 (
  input  [31:0] A,
  output [31:0] out_2
);


  assign out_2 = {A[15:0], A[31:16]};
endmodule

module u_FLIPBITS (
  input  [31:0] in_1,
  output [31:0] out_2
);

  not not_1 (out_2[0], in_1[0]);
  not not_2 (out_2[1], in_1[1]);
  not not_3 (out_2[2], in_1[2]);
  not not_4 (out_2[3], in_1[3]);
  not not_5 (out_2[4], in_1[4]);
  not not_6 (out_2[5], in_1[5]);
  not not_7 (out_2[6], in_1[6]);
  not not_8 (out_2[7], in_1[7]);
  not not_9 (out_2[8], in_1[8]);
  not not_10 (out_2[9], in_1[9]);
  not not_11 (out_2[10], in_1[10]);
  not not_12 (out_2[11], in_1[11]);
  not not_13 (out_2[12], in_1[12]);
  not not_14 (out_2[13], in_1[13]);
  not not_15 (out_2[14], in_1[14]);
  not not_16 (out_2[15], in_1[15]);
  not not_17 (out_2[16], in_1[16]);
  not not_18 (out_2[17], in_1[17]);
  not not_19 (out_2[18], in_1[18]);
  not not_20 (out_2[19], in_1[19]);
  not not_21 (out_2[20], in_1[20]);
  not not_22 (out_2[21], in_1[21]);
  not not_23 (out_2[22], in_1[22]);
  not not_24 (out_2[23], in_1[23]);
  not not_25 (out_2[24], in_1[24]);
  not not_26 (out_2[25], in_1[25]);
  not not_27 (out_2[26], in_1[26]);
  not not_28 (out_2[27], in_1[27]);
  not not_29 (out_2[28], in_1[28]);
  not not_30 (out_2[29], in_1[29]);
  not not_31 (out_2[30], in_1[30]);
  not not_32 (out_2[31], in_1[31]);
endmodule
