// Logisim project run.circ as structural Verilog: 1 circuit, main circuit main
module main (
  output [31:0] Test_Value,
  output [4:0] Test_Target,
  output halt
);

  wire CLOCK, RD_WRITE_ENABLE;
  wire [4:0] RD, RI, RS;
  wire [23:0] FETCH_ADDRESS;
  wire [31:0] INSTRUCTION, jc, RD_READ_VALUE, RD_WRITE_VALUE, RI_READ_VALUE, RS_READ_VALUE;

  RAM #(.addrWidth(24), .dataWidth(32)) ram_1 (.addr(FETCH_ADDRESS), .data(INSTRUCTION));  // open: sel, clk, ld, clr
  // Ida_Register_File ida_register_file_1: pin names not known; wires that end beside it: Test_Target, Test_Value, CLOCK, halt, RD_READ_VALUE, RS_READ_VALUE, RI_READ_VALUE, jc
  cpu_main main_1 (
    .RS_READ_VALUE(RS_READ_VALUE), .RI_READ_VALUE(RI_READ_VALUE), .RD_READ_VALUE(RD_READ_VALUE), .RS(RS),
    .RI(RI), .RD(RD), .RD_WRITE_VALUE(RD_WRITE_VALUE), .RD_WRITE_ENABLE(RD_WRITE_ENABLE), .JC_READ_VALUE(jc),
    .CLOCK(CLOCK), .INSTRUCTION(INSTRUCTION), .FETCH_ADDRESS(FETCH_ADDRESS));
  Clock clock_1 (.out(CLOCK));
endmodule
